# Fritzing sketch Schéma de montage (saved by Fritzing 0.9.3b)
breadboards: 1

parts:
  Arduino = Arduino Uno (Rev3) - ICSP
  Raspberry_Pi_1 = Raspberry Pi 3 [part_number=RPI-3-V1.2]  # not connected
  Photo_Résistance = Photocell (LDR) [package=THT]
  Résistance = Resistor [tolerance=±5% resistance=10 package=THT]
  Capteur_de_température = LM35 Temperature Sensor [package="TO92 [THT]"]
  Capteur_d'humidité = Soil Moisture Sensor

nets (from the breadboard view):
  N1: Arduino.A0, Photo_Résistance.pin_0, Résistance.Pin_1
  N2: Arduino.A2, Capteur_de_température.Vout
  N3: Arduino.A4/SDA, Capteur_d'humidité.SIG
  5V: Arduino.5V, Photo_Résistance.pin_1, Capteur_de_température.+Vs, Capteur_d'humidité.VCC
  GND: Arduino.GND, Résistance.Pin_0, Capteur_de_température.GND, Capteur_d'humidité.GND

// code stored in the sketch: sketch.ino
// Code pour récupérer les valeurs des capteurs

int serial_hum, serial_temp, serial_lum, volt_hum, volt_temp, luminosite, temperature, humidite;
float Vout, RLDR;

// Fonction setup(), appelée au démarrage de la carte Arduino
void setup()
{

  // Initialise la communication avec la raspberry
  Serial.begin(9600);
}

// Fonction loop() pour récupérer les valeurs en permanence
void loop()
{

  // Mesure la tension sur la broche A0 Humidité
  serial_hum = analogRead(A0);

  // Mesure la tension sur la broche A2 Températures
  serial_temp = analogRead(A2);

  // Mesure la tension sur la broche A4 Luminosité
  serial_lum = analogRead(A4);

  // Humidité
  volt_hum = serial_hum * 5.0;
  volt_hum /= 1023.0;

  // Voltage Température
  volt_temp = serial_temp * 5.0;
  volt_temp /= 1023.0;

  // Calcul luminosité
  Vout = (serial_lum * 0.0048828125);   // [Vout = ADC * (Vin / 1023)]
  RLDR = (10000.0 * (5 - Vout)) / Vout; // [R-LDR =(R1 (Vin - Vout))/ Vout]

  //Valeurs cohérentes

  // Humidité
  humidite = (100 - (volt_hum * 100));
  // Température
  temperature = (volt_temp - 0.5) * 100;
  // Luminosité
  luminosite = (500 / RLDR);

  // Envoi les mesure à la raspberry pour affichage et attends 250ms
  Serial.print(humidite);
  Serial.print("\t");
  Serial.print(temperature);
  Serial.print("\t");
  Serial.print(luminosite);
  Serial.print("\n");
  delay(2000);
}
